# Fritzing sketch epd (saved by Fritzing 0.9.2b)
circuit board: 7.27cm x 6.13852cm
breadboards: 1

parts:
  pyboard1 = Micro Python pyboard [part_number=PYBv10b]
  Q2 = PNP-Transistor [package="TO92 [THT]"]
  Q3 = NPN-Transistor [package="TO92 [THT]"]
  Q4 = NPN-Transistor [package="TO92 [THT]"]
  R2 = Resistor [tolerance=±5% resistance=1k package=THT]
  R3 = Resistor [tolerance=±5% resistance=10k package=THT]
  R4 = Resistor [tolerance=±5% resistance=10k package=THT]
  R5 = Resistor [tolerance=±5% resistance=10k package=THT]
  J2 = double row male pin header, 14 pins [form="♂ (male)"]
  J3 = female pin header, 2 pins [form="♀ (female)"]
  R6 = Resistor [tolerance=±5% resistance=4.7k package=THT]
  J4 = female pin header, 2 pins [form="♀ (female)"]

nets:
  N1: pyboard1.X9, J2.pin5
  N2: pyboard1.X10, J2.pin10
  N3: pyboard1.X11, J2.pin4
  N4: pyboard1.X12, J2.pin11
  N5: pyboard1.X14_GND, Q3.E, R3.Pin_0, R5.Pin_0, J3.pin1
  N6: pyboard1.X15_3V3, Q2.E, R4.Pin_1
  N7: pyboard1.X16_VIN, J3.pin2
  N8: pyboard1.Y1, J2.pin6
  N9: pyboard1.Y2, J2.pin9
  N10: pyboard1.Y3, J2.pin7
  N11: pyboard1.Y4, J2.pin8
  N12: pyboard1.Y5, J2.pin12
  N13: pyboard1.Y6, J2.pin2
  N14: pyboard1.Y7, J2.pin3
  N15: pyboard1.Y8, J2.pin13
  N16: pyboard1.Y12, R6.Pin_0
  N17: Q2.B, R2.Pin_1, R4.Pin_0
  N18: Q2.C, J2.pin14, J4.pin1
  N19: Q3.B, Q4.E, R3.Pin_1
  N20: Q3.C, J2.pin1, J4.pin2
  N21: Q4.B, R5.Pin_1, R6.Pin_1
  N22: Q4.C, R2.Pin_0

notes:
  Vin
  Gnd
  Vdd
  Vss
  0v
